// Logisim project project.circ as structural Verilog: 6 circuits, main circuit main
module main (
);

  wire reg_file_1_p1;

  // REG_file reg_file_1: pin names not known; wires that end beside it: reg_file_1_p1, reg_file_1_p1
endmodule

module REG_file (
  input  [2:0] Rs1,
  input  [2:0] Rs2,
  input  [2:0] rd,
  input  RegWrite,
  input  [31:0] BusW,
  output [31:0] BusB,
  output [31:0] BusA
);

  wire and_1_out, and_2_out, and_3_out, and_4_out, and_5_out, and_6_out, and_7_out, clock_1_out,
       decoder_1_out0, decoder_1_out1, decoder_1_out2, decoder_1_out3, decoder_1_out4, decoder_1_out5,
       decoder_1_out6, decoder_1_out7, decoder_2_out0, decoder_2_out1, decoder_2_out2, decoder_2_out3,
       decoder_2_out4, decoder_2_out5, decoder_2_out6, decoder_2_out7, decoder_3_out0, decoder_3_out1,
       decoder_3_out2, decoder_3_out3, decoder_3_out4, decoder_3_out5, decoder_3_out6, decoder_3_out7;
  wire [31:0] R1_q, R2_q, R3_q, R4_q, R5_q, R6_q, R7_q;

  Decoder #(.select(3), .enable("false")) decoder_1 (
    .out0(decoder_1_out0), .out1(decoder_1_out1), .out2(decoder_1_out2), .out3(decoder_1_out3),
    .out4(decoder_1_out4), .out5(decoder_1_out5), .out6(decoder_1_out6), .out7(decoder_1_out7), .sel(rd));
  and and_1 (and_1_out, decoder_1_out1, RegWrite);
  and and_2 (and_2_out, decoder_1_out2, RegWrite);
  and and_3 (and_3_out, decoder_1_out3, RegWrite);
  and and_4 (and_4_out, decoder_1_out4, RegWrite);
  and and_5 (and_5_out, decoder_1_out5, RegWrite);
  and and_6 (and_6_out, decoder_1_out6, RegWrite);
  and and_7 (and_7_out, decoder_1_out7, RegWrite);
  Register #(.width(32)) R1 (.D(BusW), .en(and_1_out), .Q(R1_q), .clk(clock_1_out));  // open: clr
  Register #(.width(32)) R2 (.D(BusW), .en(and_2_out), .Q(R2_q), .clk(clock_1_out));  // open: clr
  Register #(.width(32)) R3 (.D(BusW), .en(and_3_out), .Q(R3_q), .clk(clock_1_out));  // open: clr
  Register #(.width(32)) R4 (.D(BusW), .en(and_4_out), .Q(R4_q), .clk(clock_1_out));  // open: clr
  Register #(.width(32)) R5 (.D(BusW), .en(and_5_out), .Q(R5_q), .clk(clock_1_out));  // open: clr
  Register #(.width(32)) R6 (.D(BusW), .en(and_6_out), .Q(R6_q), .clk(clock_1_out));  // open: clr
  Register #(.width(32)) R7 (.D(BusW), .en(and_7_out), .Q(R7_q), .clk(clock_1_out));  // open: clr
  Clock clock_1 (.out(clock_1_out));
  Decoder #(.select(3), .enable("false")) decoder_2 (
    .out0(decoder_2_out0), .out1(decoder_2_out1), .out2(decoder_2_out2), .out3(decoder_2_out3),
    .out4(decoder_2_out4), .out5(decoder_2_out5), .out6(decoder_2_out6), .out7(decoder_2_out7), .sel(Rs1));
  assign BusA = decoder_2_out0 ? {32{1'b0}} : 32'bz;  // Controlled_Buffer controlled_buffer_1
  assign BusA = decoder_2_out1 ? R1_q : 32'bz;  // Controlled_Buffer controlled_buffer_2
  assign BusA = decoder_2_out2 ? R2_q : 32'bz;  // Controlled_Buffer controlled_buffer_3
  assign BusA = decoder_2_out3 ? R3_q : 32'bz;  // Controlled_Buffer controlled_buffer_4
  assign BusA = decoder_2_out4 ? R4_q : 32'bz;  // Controlled_Buffer controlled_buffer_5
  assign BusA = decoder_2_out5 ? R5_q : 32'bz;  // Controlled_Buffer controlled_buffer_6
  assign BusA = decoder_2_out6 ? R6_q : 32'bz;  // Controlled_Buffer controlled_buffer_7
  assign BusA = decoder_2_out7 ? R7_q : 32'bz;  // Controlled_Buffer controlled_buffer_8
  assign BusB = decoder_3_out0 ? {32{1'b0}} : 32'bz;  // Controlled_Buffer controlled_buffer_9
  assign BusB = decoder_3_out1 ? R1_q : 32'bz;  // Controlled_Buffer controlled_buffer_10
  assign BusB = decoder_3_out2 ? R2_q : 32'bz;  // Controlled_Buffer controlled_buffer_11
  assign BusB = decoder_3_out3 ? R3_q : 32'bz;  // Controlled_Buffer controlled_buffer_12
  assign BusB = decoder_3_out4 ? R4_q : 32'bz;  // Controlled_Buffer controlled_buffer_13
  assign BusB = decoder_3_out5 ? R5_q : 32'bz;  // Controlled_Buffer controlled_buffer_14
  assign BusB = decoder_3_out6 ? R6_q : 32'bz;  // Controlled_Buffer controlled_buffer_15
  assign BusB = decoder_3_out7 ? R7_q : 32'bz;  // Controlled_Buffer controlled_buffer_16
  Decoder #(.select(3), .enable("false")) decoder_3 (
    .out0(decoder_3_out0), .out1(decoder_3_out1), .out2(decoder_3_out2), .out3(decoder_3_out3),
    .out4(decoder_3_out4), .out5(decoder_3_out5), .out6(decoder_3_out6), .out7(decoder_3_out7), .sel(Rs2));
endmodule

module ALU (
  input  [31:0] in_1,
  input  [31:0] in_2,
  input  in_3,
  input  [3:0] alu_op,
  input  zero,
  output [31:0] out_6
);

  wire adder_1_cout, adder_2_cout, comparator_1_eq, comparator_1_lt, or_2_out;
  wire [31:0] adder_1_out, adder_2_out, and_1_out, and_2_out, bit_extender_1_out, bit_extender_2_out,
       negator_1_out, not_1_out, or_1_out, shifter_1_out, shifter_2_out, shifter_3_out, shifter_4_out,
       xor_1_out;

  Multiplexer #(.enable("false")) multiplexer_1 (.in0(adder_2_cout), .in1(adder_1_cout), .out(in_3), .sel(alu_op[0]));
  Negator #(.width(32)) negator_1 (.in(in_1), .out(negator_1_out));
  assign not_1_out = ~in_1;  // NOT_Gate not_1, 32 bits wide
  Adder #(.width(32)) adder_1 (.a(negator_1_out), .b(in_2), .out(adder_1_out), .cin(1'b0), .cout(adder_1_cout));
  Comparator #(.width(32)) comparator_1 (.a(in_1), .b(in_2), .eq(comparator_1_eq), .lt(comparator_1_lt));  // open: gt
  assign and_1_out = in_1 & in_2;  // AND_Gate and_1, 32 bits wide
  assign and_2_out = not_1_out & in_2;  // AND_Gate and_2, 32 bits wide
  assign or_1_out = in_1 | in_2;  // OR_Gate or_1, 32 bits wide
  assign xor_1_out = in_1 ^ in_2;  // XOR_Gate xor_1, 32 bits wide
  Adder #(.width(32)) adder_2 (.a(in_1), .b(in_2), .out(adder_2_out), .cin(1'b0), .cout(adder_2_cout));
  assign bit_extender_1_out = {{31{comparator_1_eq}}, comparator_1_eq};  // Bit_Extender bit_extender_1
  assign bit_extender_2_out = {{31{comparator_1_lt}}, comparator_1_lt};  // Bit_Extender bit_extender_2
  Shifter #(.width(32)) shifter_1 (.in(in_1), .\dist (in_2[4:0]), .out(shifter_1_out));
  Shifter #(.width(32), .shift("lr")) shifter_2 (.in(in_1), .\dist (in_2[4:0]), .out(shifter_2_out));
  Shifter #(.width(32), .shift("ar")) shifter_3 (.in(in_1), .\dist (in_2[4:0]), .out(shifter_3_out));
  Shifter #(.width(32), .shift("rr")) shifter_4 (.in(in_1), .\dist (in_2[4:0]), .out(shifter_4_out));
  Multiplexer #(.select(4), .width(32), .enable("false")) multiplexer_2 (
    .in0(and_1_out), .in1(and_2_out), .in2(or_1_out), .in3(xor_1_out), .in4(adder_2_out), .in5(adder_1_out),
    .in6(bit_extender_1_out), .in7(shifter_1_out), .in8(bit_extender_2_out), .in9(shifter_2_out),
    .in10(shifter_3_out), .in11(shifter_4_out), .out(out_6), .sel(alu_op));  // open: in12, in13, in14, in15
  or or_2 (or_2_out, out_6[0], out_6[1], out_6[2], out_6[3], out_6[4], out_6[5], out_6[6], out_6[7], out_6[8], out_6[9], out_6[10], out_6[11], out_6[12], out_6[13], out_6[14], out_6[15], out_6[16], out_6[17], out_6[18], out_6[19], out_6[20], out_6[21], out_6[22], out_6[23], out_6[24], out_6[25], out_6[26], out_6[27], out_6[28], out_6[29], out_6[30], out_6[31]);

  // Other names for the same wires on the sheet: Bb[31:0] = in_2; A[31:0] = in_1
endmodule

module CPU (
  input  in_1
);

  wire clock_1_out, clock_2_out, clock_3_out, ext_oper, mem_rea, mem_write, reg_write, zero;
  wire [1:0] Alut_source, F, PC_source, reg_des, wrbdat;
  wire [2:0] multiplexer_2_out;
  wire [3:0] alu_op;
  wire [4:0] OpCode;
  wire [4:2] Itype_IMM5;
  wire [10:5] Jtype_IMM11;
  wire [19:0] bit_extender_1_out, multiplexer_1_out, PC_2, PC___IMM__1, PC__IMM11__1, register_1_q;
  wire [31:0] alu_1_p2, bit_extender_2_out, bit_extender_4_out, Branch_less_than, IMM5___sign, IMM11___sign,
       multiplexer_3_out, multiplexer_5_out, multiplier_1_out, multiplier_2_out, ram_1_data, reg_file_1_busa,
       reg_file_1_busb;
  wire [31:20] adder_2_out, adder_3_out;

  assign bit_extender_1_out = {{17{1'b0}}, Jtype_IMM11[10:8]};  // Bit_Extender bit_extender_1
  Multiplexer #(.select(2), .width(20), .enable("false")) multiplexer_1 (
    .in0(PC__IMM11__1), .in1(PC___IMM__1), .in2(bit_extender_1_out), .in3(PC_2), .out(multiplexer_1_out),
    .sel(PC_source));
  assign bit_extender_2_out = {{12{1'b0}}, PC_2};  // Bit_Extender bit_extender_2
  Register #(.width(20)) register_1 (
    .D(multiplexer_1_out), .en(1'b1), .Q(register_1_q), .clk(clock_1_out));  // open: clr
  Clock clock_1 (.out(clock_1_out));
  Adder #(.width(20)) adder_1 (.a(register_1_q), .b(20'h2), .out(PC_2));  // open: cin, cout
  Multiplier #(.width(32)) multiplier_1 (.a(IMM5___sign), .b(32'h2), .out(multiplier_1_out));  // open: cin, cout
  Multiplier #(.width(32)) multiplier_2 (.a(IMM11___sign), .b(32'h2), .out(multiplier_2_out));  // open: cin, cout
  Adder #(.width(32)) adder_2 (
    .a(multiplier_1_out), .b(bit_extender_2_out), .out({adder_2_out, PC___IMM__1}));  // open: cin, cout
  Adder #(.width(32)) adder_3 (
    .a(bit_extender_2_out), .b(multiplier_2_out), .out({adder_3_out, PC__IMM11__1}));  // open: cin, cout
  ROM #(.addrWidth(20), .dataWidth(16)) rom_1 (
    .addr(register_1_q), .data({OpCode, Jtype_IMM11, Itype_IMM5, F}));  // open: sel
  PC_control pc_control_1 (.Op_Code(OpCode), .Branch(Branch_less_than), .in_2(PC_source), .Zero(zero));
  Multiplexer #(.select(2), .width(3), .enable("false")) multiplexer_2 (
    .in0(Itype_IMM5), .in1(Jtype_IMM11[7:5]), .in2(3'b111), .out(multiplexer_2_out), .sel(reg_des));  // open: in3
  REG_file reg_file_1 (
    .Rs1(Jtype_IMM11[10:8]), .Rs2(Jtype_IMM11[7:5]), .rd(multiplexer_2_out), .RegWrite(reg_write),
    .BusW(multiplexer_5_out), .BusA(reg_file_1_busa), .BusB(reg_file_1_busb));
  Clock clock_2 (.out(clock_2_out));
  assign IMM5___sign = {{27{Itype_IMM5[4]}}, {Itype_IMM5, F}};  // Bit_Extender bit_extender_3
  assign bit_extender_4_out = {{27{1'b0}}, {Itype_IMM5, F}};  // Bit_Extender bit_extender_4
  assign IMM11___sign = {{21{Jtype_IMM11[10]}}, {Jtype_IMM11, Itype_IMM5, F}};  // Bit_Extender bit_extender_5
  Multiplexer #(.width(32), .enable("false")) multiplexer_3 (
    .in0(IMM5___sign), .in1(bit_extender_4_out), .out(multiplexer_3_out), .sel(ext_oper));
  // ALU alu_1: pin names not known; wires that end beside it: reg_file_1_busa, alu_1_p2, zero, alu_op, Branch_less_than
  Multiplexer #(.select(2), .width(32), .enable("false")) multiplexer_4 (
    .in0(reg_file_1_busb), .in1(IMM5___sign), .in2(IMM11___sign), .in3(multiplexer_3_out), .out(alu_1_p2),
    .sel(Alut_source));
  Control control_1 (
    .Opcode(OpCode), .reg_write(reg_write), .ext_OP(ext_oper), .ALU_src(Alut_source), .Mem_Write(mem_write),
    .Mem_Read(mem_rea), .in_2(F), .reg_dest(reg_des), .ALU_opeartion(alu_op), .Write_back_data(wrbdat));  // open: out_3
  Clock clock_3 (.out(clock_3_out));
  RAM #(.addrWidth(20), .dataWidth(32), .bus("separate")) ram_1 (
    .addr(Branch_less_than[19:0]), .din(reg_file_1_busb), .data(ram_1_data), .str(mem_write),
    .clk(clock_3_out), .ld(mem_rea));  // open: sel, clr
  Multiplexer #(.select(2), .width(32), .enable("false")) multiplexer_5 (
    .in0(Branch_less_than), .in1(ram_1_data), .out(multiplexer_5_out), .sel(wrbdat));  // open: in2, in3
  Bit_Extender #(.in_width(20)) bit_extender_6 (.in(PC_2));  // open: out

  // Other names for the same wires on the sheet: Itype_IMM5[1:0] = F; Jtype_IMM11[4:0] = {Itype_IMM5, F};
  //   RW_RD[2:0] = Itype_IMM5; RB[2:0] = Jtype_IMM11[7:5]; RA[2:0] = Jtype_IMM11[10:8]

  // Notes on the sheet:
  //   Branch
  //   Instrucation memory
  //   registerDS
  //   Extend operation
  //   buBselect
  //   Branch
  //   Data memory
  //   memory write
  //   read
  //   write back data
endmodule

module Control (
  input  [4:0] Opcode,
  input  [1:0] in_2,
  output [9:0] out_3,
  output [1:0] reg_dest,
  output reg_write,
  output ext_OP,
  output [1:0] ALU_src,
  output Mem_Write,
  output [1:0] Write_back_data,
  output Mem_Read,
  output [3:0] ALU_opeartion
);

  // Probe on Opcode
  // Probe on {Opcode, in_2}
  ROM #(.addrWidth(5), .dataWidth(10)) rom_1 (
    .addr(Opcode), .data({out_3[9:8], Mem_Read, Mem_Write, ALU_src, ext_OP, out_3[2:0]}));  // open: sel
  ROM #(.addrWidth(7), .dataWidth(4)) rom_2 (.addr({Opcode, in_2}), .data(ALU_opeartion));  // open: sel
  // Probe on ALU_opeartion

  assign out_3[7:3] = {Mem_Read, Mem_Write, ALU_src, ext_OP};
  assign reg_dest = out_3[1:0];
  assign reg_write = out_3[2];
  assign Write_back_data = out_3[9:8];

  // Notes on the sheet:
  //   contents of rom_1 (hex, n*v repeats v):
  //   5 5 0 0 1c 35 14 14 1c 1c 20 20 0 14 14 14 8 8 158 98
  //   contents of rom_2 (hex, n*v repeats v):
  //   0 1 2 3 0 1 2 3 12*0 4*1 4*2 4*3 4*4 4*5 4*6 4*8 4*7 4*9 4*a 4*0 8*5
endmodule

module PC_control (
  input  [4:0] Op_Code,
  input  [1:0] in_2,
  input  Zero,
  input  [31:0] Branch
);

  ROM #(.addrWidth(7), .dataWidth(2)) rom_1 (.addr({Zero, Branch[0], Op_Code}), .data(in_2));  // open: sel
endmodule
